// Logisim project FSM_Light.circ as structural Verilog: 1 circuit, main circuit main
module main (
);

  wire and_1_out, and_2_out, and_3_out, clock_1_out, clock_2_out, Input_w, or_1_out, output__NS_Signal,
       output__WE_Signal, SC0_q, SC0_qn, SC1_q, SC1_qn, xnor_1_out;

  Clock clock_1 (.out(clock_1_out));
  Clock clock_2 (.out(clock_2_out));
  D_Flip_Flop SC0 (.clk(clock_1_out), .D(or_1_out), .Q(SC0_q), .Qn(SC0_qn));  // open: preset, en, reset
  D_Flip_Flop SC1 (.clk(clock_2_out), .D(and_1_out), .Q(SC1_q), .Qn(SC1_qn));  // open: preset, en, reset
  xnor xnor_1 (xnor_1_out, Input_w, SC0_q);
  and and_1 (and_1_out, SC1_qn, Input_w);
  and and_2 (and_2_out, SC1_q, SC0_qn);
  and and_3 (and_3_out, xnor_1_out, SC1_qn);
  and and_4 (output__NS_Signal, SC0_qn, SC1_qn);
  and and_5 (output__WE_Signal, SC0_q, SC1_qn);
  or or_1 (or_1_out, and_2_out, and_3_out);
endmodule
